# Fritzing sketch NK Rover (saved by Fritzing 0.9.3b)
circuit board: 8.46667cm x 5.64444cm
breadboards: 1

parts:
  M1 = DC Motor
  M2 = DC Motor
  Buzzer = Piezo Speaker
  LED1 = LEDs [package=led10mm]
  LED2 = LEDs [package=led10mm]
  R1 = Resistor [tolerance=±5% resistance=220 package="0402 [SMD]"]
  Raspberry_Pi_1 = Raspberry Pi 3 [part_number=RPI-3-V1.2]
  S1 = Pushbutton [package="[SMD]"]
  S2 = Pushbutton [package="[SMD]"]
  Composant1 = Motor Driver 1A Dual TB6612FNG
  LCD1 = LCD screen
  R2 = Resistor [tolerance=±5% resistance=220 package="2512 [SMD]"]
  R3 = Resistor [tolerance=±5% resistance=220 package="1206 [SMD]"]

nets:
  N1: M1.pin_1, Composant1.A01
  N2: M1.pin_2, Composant1.A02
  N3: M2.pin_1, Composant1.B02
  N4: M2.pin_2, Composant1.B01
  3V3: Buzzer.pin1, R1.Pin_0, Raspberry_Pi_1.3v3, Raspberry_Pi_1.3V3, Composant1.VCC, Composant1.STBY, R2.Pin_1
  N5: Buzzer.pin2, Raspberry_Pi_1.GPIO22
  N6: LED1.C, Raspberry_Pi_1.GPIO23
  N7: LED1.A, LED2.C
  N8: LED2.A, R1.Pin_1
  N9: Raspberry_Pi_1.GPIO4, Composant1.PWMB
  N10: Raspberry_Pi_1.GPIO17, Composant1.AIN1
  N11: Raspberry_Pi_1.GPIO27, Composant1.PWMA
  N12: Raspberry_Pi_1.GPIO10, LCD1.V0
  N13: Raspberry_Pi_1.GPIO9, LCD1.RS
  N14: Raspberry_Pi_1.GPIO11, LCD1.E
  N15: Raspberry_Pi_1.GPIO5, LCD1.DB6
  N16: Raspberry_Pi_1.GPIO6, LCD1.DB7
  N17: Raspberry_Pi_1.GPIO12, LCD1.Red_LED
  GND: Raspberry_Pi_1.GND, Composant1.GND, LCD1.VSS, LCD1.R/W, R3.Pin_1
  N18: Raspberry_Pi_1.GPIO7, LCD1.DB5
  N19: Raspberry_Pi_1.GPIO8, LCD1.DB4
  N20: Raspberry_Pi_1.GPIO25, Raspberry_Pi_1.GPIO24, S1.Pin_1, S1.Pin_2, S1.Pin_3, S1.Pin_4, S2.Pin_1, S2.Pin_2, S2.Pin_3, S2.Pin_4, R2.Pin_0
  N21: Raspberry_Pi_1.GPIO18, Composant1.AIN2
  N22: Raspberry_Pi_1.GPIO15, Composant1.BIN1
  N23: Raspberry_Pi_1.GPIO14, Composant1.BIN2
  5V: Raspberry_Pi_1.5V, Composant1.VM, LCD1.VDD
  N24: LCD1.K, R3.Pin_0

custom parts:
  LCD screen: A standard character display, usually with 2x16 characters. Comes in many colors.
